// Logisim project control_logic.circ as structural Verilog: 1 circuit, main circuit control_logic
module control_logic (
  input  [31:0] inst,
  input  BrEq,
  input  BrLt,
  output PCSel,
  output RegWEn,
  output [2:0] ImmSel,
  output BrUn,
  output ASel,
  output BSel,
  output [3:0] ALUSel,
  output MemRW,
  output [1:0] WBSel,
  output [3:0] out_13
);

  wire and_1_out, and_2_out, and_3_out, and_4_out, and_6_out, and_7_out, and_8_out, and_9_out, and_10_out,
       and_11_out, and_12_out, and_13_out, and_14_out, comparator_1_eq, comparator_2_eq, comparator_3_eq,
       comparator_4_eq, comparator_5_eq, comparator_6_eq, comparator_7_eq, comparator_8_eq, comparator_9_eq,
       comparator_10_eq, comparator_11_eq, comparator_12_eq, comparator_13_eq, comparator_14_eq,
       comparator_15_eq, comparator_16_eq, comparator_17_eq, comparator_18_eq, comparator_19_eq,
       comparator_20_eq, comparator_21_eq, comparator_22_eq, comparator_23_eq, comparator_24_eq,
       comparator_25_eq, comparator_26_eq, comparator_27_eq, comparator_28_eq, comparator_29_eq,
       comparator_30_eq, comparator_31_eq, comparator_32_eq, comparator_33_eq, comparator_34_eq,
       comparator_35_eq, comparator_36_eq, comparator_37_eq, comparator_38_eq, comparator_39_eq,
       comparator_40_eq, comparator_41_eq, comparator_42_eq, comparator_43_eq, comparator_44_eq,
       comparator_45_eq, comparator_46_eq, comparator_47_eq, comparator_48_eq, comparator_49_eq,
       comparator_50_eq, comparator_51_eq, comparator_52_eq, comparator_53_eq, or_1_out, or_2_out;
  wire [0:0] and_5_out;
  wire [1:0] multiplexer_22_out, multiplexer_23_out, multiplexer_24_out, or_7_out;
  wire [2:0] multiplexer_1_out, multiplexer_2_out, multiplexer_3_out, multiplexer_4_out, multiplexer_5_out,
       multiplexer_21_out, multiplexer_26_out;
  wire [3:0] addi, bsel13, DIVU8, MULH14, MULHU11, multiplexer_11_out, MULU10, OR2, REMU9, SLL6, SLT7, SRA5,
       SRL4, Sub12, typeI, typeR, XOR3;

  Comparator #(.width(7)) comparator_1 (.a(7'b0010011), .b(inst[6:0]), .eq(comparator_1_eq));  // open: gt, lt
  Comparator #(.width(7)) comparator_2 (.a(7'b0100011), .b(inst[6:0]), .eq(comparator_2_eq));  // open: gt, lt
  Comparator #(.width(7)) comparator_3 (.a(7'b1100011), .b(inst[6:0]), .eq(comparator_3_eq));  // open: gt, lt
  Comparator #(.width(7)) comparator_4 (.a(7'b0010111), .b(inst[6:0]), .eq(comparator_4_eq));  // open: gt, lt
  Comparator #(.width(7)) comparator_5 (.a(7'b0110111), .b(inst[6:0]), .eq(comparator_5_eq));  // open: gt, lt
  Comparator #(.width(7)) comparator_6 (.a(7'b1100111), .b(inst[6:0]), .eq(comparator_6_eq));  // open: gt, lt
  Comparator #(.width(7)) comparator_7 (.a(7'b0000011), .b(inst[6:0]), .eq(comparator_7_eq));  // open: gt, lt
  Comparator #(.width(7)) comparator_8 (.a(7'b1101111), .b(inst[6:0]), .eq(comparator_8_eq));  // open: gt, lt
  Comparator #(.width(7)) comparator_9 (.a(7'b0110011), .b(inst[6:0]), .eq(comparator_9_eq));  // open: gt, lt
  Comparator #(.width(7)) comparator_10 (.a(7'b0000011), .b(inst[6:0]), .eq(comparator_10_eq));  // open: gt, lt
  Comparator #(.width(7)) comparator_11 (.a(7'b0010011), .b(inst[6:0]), .eq(comparator_11_eq));  // open: gt, lt
  Comparator #(.width(7)) comparator_12 (.a(7'b0010111), .b(inst[6:0]), .eq(comparator_12_eq));  // open: gt, lt
  or or_1 (or_1_out, comparator_7_eq, comparator_6_eq, comparator_1_eq);
  Multiplexer #(.width(3), .enable("false")) multiplexer_1 (
    .in0(3'b000), .in1(3'b001), .out(multiplexer_1_out), .sel(comparator_2_eq));
  or or_2 (or_2_out, comparator_4_eq, comparator_5_eq);
  Comparator #(.width(7)) comparator_13 (.a(7'b1101111), .b(inst[6:0]), .eq(comparator_13_eq));  // open: gt, lt
  Multiplexer #(.width(3), .enable("false")) multiplexer_2 (
    .in0(3'b000), .in1(3'b000), .out(multiplexer_2_out), .sel(or_1_out));
  Multiplexer #(.width(3), .enable("false")) multiplexer_3 (
    .in0(3'b000), .in1(3'b010), .out(multiplexer_3_out), .sel(comparator_3_eq));
  Multiplexer #(.width(3), .enable("false")) multiplexer_4 (
    .in0(3'b000), .in1(3'b011), .out(multiplexer_4_out), .sel(or_2_out));
  or or_3 (RegWEn, comparator_15_eq, comparator_9_eq, comparator_10_eq, comparator_13_eq, comparator_11_eq, comparator_12_eq, comparator_14_eq);
  Comparator #(.width(7)) comparator_14 (.a(7'b0110111), .b(inst[6:0]), .eq(comparator_14_eq));  // open: gt, lt
  Multiplexer #(.width(3), .enable("false")) multiplexer_5 (
    .in0(3'b000), .in1(3'b100), .out(multiplexer_5_out), .sel(comparator_8_eq));
  assign ImmSel = multiplexer_2_out | multiplexer_1_out | multiplexer_3_out | multiplexer_4_out | multiplexer_5_out;  // OR_Gate or_4, 3 bits wide
  Comparator #(.width(7)) comparator_15 (.a(7'b1100111), .b(inst[6:0]), .eq(comparator_15_eq));  // open: gt, lt
  Comparator #(.width(3)) comparator_16 (.a(3'b100), .b(inst[14:12]), .eq(comparator_16_eq));  // open: gt, lt
  Comparator #(.width(7)) comparator_17 (.a(inst[31:25]), .b({7{1'b0}}), .eq(comparator_17_eq));  // open: gt, lt
  Comparator #(.width(3)) comparator_18 (.a(3'b110), .b(inst[14:12]), .eq(comparator_18_eq));  // open: gt, lt
  Comparator #(.width(7)) comparator_19 (.a(inst[31:25]), .b({7{1'b0}}), .eq(comparator_19_eq));  // open: gt, lt
  and and_1 (and_1_out, comparator_16_eq, comparator_17_eq);
  and and_2 (and_2_out, comparator_18_eq, comparator_19_eq);
  Comparator #(.width(3)) comparator_20 (.a(3'b101), .b(inst[14:12]), .eq(comparator_20_eq));  // open: gt, lt
  Comparator #(.width(7)) comparator_21 (.a(inst[31:25]), .b(7'b0100000), .eq(comparator_21_eq));  // open: gt, lt
  and and_3 (and_3_out, comparator_20_eq, comparator_21_eq);
  Multiplexer #(.width(4), .enable("false")) multiplexer_6 (.in0(4'b0000), .in1(4'b0011), .out(XOR3), .sel(and_1_out));
  Comparator #(.width(3)) comparator_22 (.a(3'b101), .b(inst[14:12]), .eq(comparator_22_eq));  // open: gt, lt
  Comparator #(.width(7)) comparator_23 (.a(inst[31:25]), .b({7{1'b0}}), .eq(comparator_23_eq));  // open: gt, lt
  Comparator #(.width(3)) comparator_24 (.a(3'b111), .b(inst[14:12]), .eq(comparator_24_eq));  // open: gt, lt
  Comparator #(.width(7)) comparator_25 (.a(inst[31:25]), .b({7{1'b0}}), .eq(comparator_25_eq));  // open: gt, lt
  Multiplexer #(.width(4), .enable("false")) multiplexer_7 (.in0(4'b0000), .in1(4'b0010), .out(OR2), .sel(and_2_out));
  and and_4 (and_4_out, comparator_22_eq, comparator_23_eq);
  Comparator #(.width(3)) comparator_26 (.a(3'b000), .b(inst[14:12]), .eq(comparator_26_eq));  // open: gt, lt
  Comparator #(.width(3)) comparator_27 (.a(3'b000), .b(inst[14:12]), .eq(comparator_27_eq));  // open: gt, lt
  Comparator #(.width(7)) comparator_28 (.a(inst[31:25]), .b({7{1'b0}}), .eq(comparator_28_eq));  // open: gt, lt
  and and_5 (and_5_out[0], comparator_24_eq, comparator_25_eq);
  Multiplexer #(.width(4), .enable("false")) multiplexer_8 (.in0(4'b0000), .in1(4'b0101), .out(SRA5), .sel(and_3_out));
  and and_6 (and_6_out, comparator_27_eq, comparator_28_eq);
  Multiplexer #(.width(4), .enable("false")) multiplexer_9 (.in0(4'b0000), .in1(4'b0100), .out(SRL4), .sel(and_4_out));
  Multiplexer #(.width(4), .enable("false")) multiplexer_10 (
    .in0(4'b0000), .in1(4'b0000), .out(addi), .sel(comparator_26_eq));
  Multiplexer #(.width(4), .enable("false")) multiplexer_11 (
    .in0(4'b0000), .in1(4'b0000), .out(multiplexer_11_out), .sel(and_6_out));
  Comparator #(.width(3)) comparator_29 (.a(3'b010), .b(inst[14:12]), .eq(comparator_29_eq));  // open: gt, lt
  Comparator #(.width(7)) comparator_30 (.a(inst[31:25]), .b({7{1'b0}}), .eq(comparator_30_eq));  // open: gt, lt
  Comparator #(.width(3)) comparator_31 (.a(3'b001), .b(inst[14:12]), .eq(comparator_31_eq));  // open: gt, lt
  Comparator #(.width(7)) comparator_32 (.a(inst[31:25]), .b({7{1'b0}}), .eq(comparator_32_eq));  // open: gt, lt
  and and_7 (and_7_out, comparator_29_eq, comparator_30_eq);
  and and_8 (and_8_out, comparator_31_eq, comparator_32_eq);
  assign typeR = multiplexer_11_out | {3'b000, and_5_out[0]} | OR2 | XOR3 | SRL4 | SRA5 | SLL6 | SLT7 | DIVU8 | REMU9 | MULU10 | MULHU11 | Sub12 | MULH14;  // OR_Gate or_5, 4 bits wide
  Comparator #(.width(7)) comparator_33 (.a(7'b1100011), .b(inst[6:0]), .eq(comparator_33_eq));  // open: gt, lt
  Comparator #(.width(7)) comparator_34 (.a(7'b1100111), .b(inst[6:0]), .eq(comparator_34_eq));  // open: gt, lt
  Comparator #(.width(7)) comparator_35 (.a(7'b1101111), .b(inst[6:0]), .eq(comparator_35_eq));  // open: gt, lt
  Multiplexer #(.width(4), .enable("false")) multiplexer_12 (.in0(4'b0000), .in1(4'b0111), .out(SLT7), .sel(and_7_out));
  Multiplexer #(.width(4), .enable("false")) multiplexer_13 (.in0(4'b0000), .in1(4'b0110), .out(SLL6), .sel(and_8_out));
  or or_6 (PCSel, comparator_33_eq, comparator_34_eq, comparator_35_eq);
  Comparator #(.width(7)) comparator_36 (.a(7'b0110111), .b(inst[6:0]), .eq(comparator_36_eq));  // open: gt, lt
  Comparator #(.width(3)) comparator_37 (.a(3'b001), .b(inst[14:12]), .eq(comparator_37_eq));  // open: gt, lt
  Comparator #(.width(7)) comparator_38 (.a(inst[31:25]), .b(7'b0000001), .eq(comparator_38_eq));  // open: gt, lt
  Comparator #(.width(3)) comparator_39 (.a(3'b000), .b(inst[14:12]), .eq(comparator_39_eq));  // open: gt, lt
  Comparator #(.width(7)) comparator_40 (.a(inst[31:25]), .b(7'b0100000), .eq(comparator_40_eq));  // open: gt, lt
  Comparator #(.width(3)) comparator_41 (.a(3'b011), .b(inst[14:12]), .eq(comparator_41_eq));  // open: gt, lt
  Comparator #(.width(7)) comparator_42 (.a(inst[31:25]), .b(7'b0000001), .eq(comparator_42_eq));  // open: gt, lt
  and and_9 (and_9_out, comparator_37_eq, comparator_38_eq);
  and and_10 (and_10_out, comparator_39_eq, comparator_40_eq);
  Comparator #(.width(3)) comparator_43 (.a(3'b111), .b(inst[14:12]), .eq(comparator_43_eq));  // open: gt, lt
  Comparator #(.width(7)) comparator_44 (.a(inst[31:25]), .b(7'b0000001), .eq(comparator_44_eq));  // open: gt, lt
  Comparator #(.width(3)) comparator_45 (.a(3'b000), .b(inst[14:12]), .eq(comparator_45_eq));  // open: gt, lt
  Comparator #(.width(7)) comparator_46 (.a(inst[31:25]), .b(7'b0000001), .eq(comparator_46_eq));  // open: gt, lt
  and and_11 (and_11_out, comparator_41_eq, comparator_42_eq);
  Comparator #(.width(3)) comparator_47 (.a(3'b101), .b(inst[14:12]), .eq(comparator_47_eq));  // open: gt, lt
  Comparator #(.width(7)) comparator_48 (.a(inst[31:25]), .b(7'b0000001), .eq(comparator_48_eq));  // open: gt, lt
  and and_12 (and_12_out, comparator_43_eq, comparator_44_eq);
  and and_13 (and_13_out, comparator_45_eq, comparator_46_eq);
  Multiplexer #(.width(4), .enable("false")) multiplexer_14 (
    .in0(4'b0000), .in1(4'b1101), .out(bsel13), .sel(comparator_36_eq));
  and and_14 (and_14_out, comparator_47_eq, comparator_48_eq);
  Multiplexer #(.width(4), .enable("false")) multiplexer_15 (
    .in0(4'b0000), .in1(4'b1011), .out(MULHU11), .sel(and_11_out));
  Multiplexer #(.width(4), .enable("false")) multiplexer_16 (
    .in0(4'b0000), .in1(4'b1110), .out(MULH14), .sel(and_9_out));
  Multiplexer #(.width(4), .enable("false")) multiplexer_17 (
    .in0(4'b0000), .in1(4'b1100), .out(Sub12), .sel(and_10_out));
  Multiplexer #(.width(4), .enable("false")) multiplexer_18 (
    .in0(4'b0000), .in1(4'b1001), .out(REMU9), .sel(and_12_out));
  Multiplexer #(.width(4), .enable("false")) multiplexer_19 (
    .in0(4'b0000), .in1(4'b1010), .out(MULU10), .sel(and_13_out));
  Multiplexer #(.width(4), .enable("false")) multiplexer_20 (
    .in0(4'b0000), .in1(4'b1000), .out(DIVU8), .sel(and_14_out));
  Comparator #(.width(7)) comparator_49 (.a(7'b0100000), .b(inst[31:25]), .eq(comparator_49_eq));  // open: gt, lt
  Multiplexer #(.width(3), .enable("false")) multiplexer_21 (
    .in0(3'b101), .in1(3'b011), .out(multiplexer_21_out), .sel(comparator_49_eq));
  Comparator #(.width(7)) comparator_50 (.a(7'b0110011), .b(inst[6:0]), .eq(comparator_50_eq));  // open: gt, lt
  Comparator #(.width(7)) comparator_51 (.a(7'b0010011), .b(inst[6:0]), .eq(comparator_51_eq));  // open: gt, lt
  Multiplexer #(.width(2), .enable("false")) multiplexer_22 (
    .in0(2'b00), .in1(2'b01), .out(multiplexer_22_out), .sel(comparator_52_eq));
  Comparator #(.width(7)) comparator_52 (.a(7'b0110111), .b(inst[6:0]), .eq(comparator_52_eq));  // open: gt, lt
  Multiplexer #(.width(2), .enable("false")) multiplexer_23 (
    .in0(2'b00), .in1(2'b11), .out(multiplexer_23_out), .sel(comparator_50_eq));
  Multiplexer #(.width(2), .enable("false")) multiplexer_24 (
    .in0(2'b00), .in1(2'b10), .out(multiplexer_24_out), .sel(comparator_51_eq));
  Comparator #(.width(3)) comparator_53 (.a(3'b101), .b(inst[14:12]), .eq(comparator_53_eq));  // open: gt, lt
  Multiplexer #(.select(3), .width(4), .enable("false")) multiplexer_25 (
    .in0(4'b0000), .in1(4'b0110), .in2(4'b0111), .in3(4'b0101), .in4(4'b0011), .in5(4'b0100), .in6(4'b0010),
    .in7(4'b0001), .out(typeI), .sel(multiplexer_26_out));
  Multiplexer #(.width(3), .enable("false")) multiplexer_26 (
    .in0(inst[14:12]), .in1(multiplexer_21_out), .out(multiplexer_26_out), .sel(comparator_53_eq));
  Multiplexer #(.select(2), .width(4), .enable("false")) multiplexer_27 (
    .in0(4'b0000), .in1(bsel13), .in2(typeI), .in3(typeR), .out(ALUSel), .sel(or_7_out));
  assign or_7_out = multiplexer_23_out | multiplexer_24_out | multiplexer_22_out;  // OR_Gate or_7, 2 bits wide

  // Other names for the same wires on the sheet: func3[2:0] = inst[14:12]; func7[6:0] = inst[31:25];
  //   opcode[6:0] = inst[6:0]

  // Notes on the sheet:
  //   INPUTS to your circuit
  //   DON'T CHANGE THE LOCATIONS OF THE INPUTS AND OUTPUTS!
  //   OUTPUT from your circuit
endmodule
