// Logisim project cpu.circ as structural Verilog: 1 circuit, main circuit main
module main (
  input  [31:0] INSTRUCTION,
  input  CLOCK,
  output [31:0] PROGRAM_COUNTER,
  output [31:0] ra,
  output [31:0] sp,
  output [31:0] t0,
  output [31:0] t1,
  output [31:0] t2,
  output [31:0] s0,
  output [31:0] s1,
  output [31:0] a0
);

  wire [31:0] adder_1_out, RegFile_read_data_1, RegFile_read_data_2;

  control_logic control_logic_1 (.inst(INSTRUCTION));  // open: BSel, BrUn, RegWEn, ImmSel, ASel, PCSel, BrLt, BrEq, ALUSel, MemRW, WBSel, out_13
  Adder #(.width(32)) adder_1 (.a(PROGRAM_COUNTER), .b(32'h4), .out(adder_1_out));  // open: cin, cout
  Register #(.width(32)) PC (.D(adder_1_out), .clk(CLOCK), .Q(PROGRAM_COUNTER));  // open: en, clr
  // imm_gen ImmGen: pin names not known
  regfile_main RegFile (
    .Read_Data_1(RegFile_read_data_1), .Read_Data_2(RegFile_read_data_2), .ra(ra), .sp(sp), .t0(t0), .t1(t1),
    .t2(t2), .s0(s0), .s1(s1), .a0(a0), .RegWEn(1'b1), .clk(CLOCK));  // open: rs2, rd, rs1, Write_Data, in_5
  alu Arithmetic_Logic_Unit (.A(RegFile_read_data_1), .B(RegFile_read_data_2));  // open: ALUSel, Result
  // branch_comp branch_comp_1: pin names not known
  // mem_main DMEM: pin names not known

  // Other names for the same wires on the sheet: clk = CLOCK

  // Notes on the sheet:
  //   Output
  //   IMEM (do **NOT** move this)
  //   Inputs
  //   It is OK to move the PC, RegFile, ALU, MEM, Branch Comp, Imm Gen, and Control Logic to wherever is most convenient for you when constructing your CPU, and to delete this text
  //   Inputs/Outputs for testing. Do **NOT** move these.
endmodule
