// Logisim project imm_gen.circ as structural Verilog: 1 circuit, main circuit imm_gen
module imm_gen (
  input  [31:0] inst,
  input  [2:0] ImmSel,
  output [31:0] imm
);

  Multiplexer #(.select(3), .width(32), .enable("false")) multiplexer_1 (
    .in0({{20{1'b0}}, inst[31:20]}), .in1({{20{1'b0}}, inst[31:25], inst[11:7]}),
    .in2({{19{1'b0}}, inst[31], inst[7], inst[30:25], inst[11:8], 1'b0}), .in3({inst[31:12], {12{1'b0}}}),
    .in4({{11{1'b0}}, inst[31], inst[19:12], inst[20], inst[30:21], 1'b0}), .out(imm), .sel(ImmSel));  // open: in5, in6, in7

  // Other names for the same wires on the sheet: s[11:0] = {inst[31:25], inst[11:7]};
  //   sb[12:1] = {inst[31], inst[7], inst[30:25], inst[11:8]}; u[31:12] = inst[31:12];
  //   uj[20:1] = {inst[31], inst[19:12], inst[20], inst[30:21]}; I[11:0] = inst[31:20]

  // Notes on the sheet:
  //   INPUTS to your circuit
  //   DON'T CHANGE THE LOCATIONS OF THE INPUTS AND OUTPUTS!
  //   OUTPUT from your circuit
endmodule
